// Logisim project assignment 7 mini automation system.circ as structural Verilog: 1 circuit, main circuit main
module main (
  input  INPUT,
  output out_2
);

  wire clock_1_out;

  Clock clock_1 (.out(clock_1_out));
  D_Flip_Flop d_ff_1 (.clk(clock_1_out), .D(INPUT), .Q(out_2));  // open: Qn, preset, en, reset

  // Notes on the sheet:
  //   CLOCK 1Hz
  //   CAR DETECTION (C)
endmodule
