// Logisim project assignment 9 code to gate explainer.circ as structural Verilog: 1 circuit, main circuit main
module main (
  input  in_1,
  input  in_2,
  output out_3
);

  wire and_1_out, not_1_out;

  not not_1 (not_1_out, in_2);
  and and_1 (and_1_out, in_1, not_1_out);
  Multiplexer multiplexer_1 (.in0(in_1), .in1(in_2), .out(out_3), .sel(and_1_out));  // open: en
endmodule
